# Fritzing sketch sketch (saved by Fritzing 0.9.3b)
breadboards: 1

parts:
  R1 = Resistor [tolerance=±20% resistance=470 package=THT]
  Part1 = Photon
  R2 = Resistor [tolerance=±20% resistance=470 package=THT]
  hc-sr1 = hc-sr04
  Squix1 = OLED 0.96" 128x64 I2C SSD1306

nets:
  N1: R1.Pin_0, Part1.D5, R2.Pin_0
  GND: R1.Pin_1, Part1.GND, hc-sr1.GND, Squix1.GND
  VCC: Part1.VIN, hc-sr1.VCC, Squix1.VCC
  N2: Part1.D0, Squix1.SCA
  N3: Part1.D1, Squix1.SCL
  N4: Part1.D4, hc-sr1.Trig
  N5: R2.Pin_1, hc-sr1.Echo
